// Logisim project 001.circ as structural Verilog: 1 circuit, main circuit main
module main (
  input  Z0,
  output Y0
);

  wire _0_q, _1_q, clock_1_out, nand_1_out, nand_2_out, nand_3_out, nand_4_out, nand_5_out, not_1_out,
       not_2_out, not_3_out, reset_out;

  not not_1 (not_1_out, Z0);
  Clock clock_1 (.out(clock_1_out));
  nand nand_1 (nand_1_out, Z0, _1_q);
  nand nand_2 (nand_2_out, not_1_out, not_3_out);
  J_K_Flip_Flop _0 (
    .J(nand_3_out), .clk(clock_1_out), .K(nand_4_out), .Q(_0_q), .reset(reset_out));  // open: Qn, preset, en
  nand nand_3 (nand_3_out, nand_1_out, nand_2_out);
  nand nand_4 (nand_4_out, not_1_out, _1_q);
  Button reset (.out(reset_out));
  nand nand_5 (nand_5_out, _0_q, not_1_out);
  not not_2 (not_2_out, nand_5_out);
  not not_3 (not_3_out, _1_q);
  J_K_Flip_Flop _1 (.J(not_2_out), .clk(clock_1_out), .K(_0_q), .Q(_1_q), .reset(reset_out));  // open: Qn, preset, en
  and and_1 (Y0, _0_q, _1_q);
endmodule
