// Logisim project 00110.circ as structural Verilog: 1 circuit, main circuit main
module main (
  input  in_1
);

  wire _0_q, _1_q, _1_qn, _2_q, button_1_out, clock_1_out, nand_1_out, nand_2_out, nand_3_out, nand_4_out,
       nand_5_out, nand_6_out, nand_7_out, nand_8_out, not_1_out, not_2_out, not_3_out, not_4_out, not_5_out,
       not_6_out, not_7_out, not_8_out;

  Button button_1 (.out(button_1_out));
  Clock clock_1 (.out(clock_1_out));
  not not_1 (not_1_out, in_1);
  not not_2 (not_2_out, _0_q);
  not not_3 (not_3_out, in_1);
  nand nand_1 (nand_1_out, not_1_out, not_2_out);
  J_K_Flip_Flop _2 (
    .J(not_4_out), .clk(clock_1_out), .K(nand_1_out), .Q(_2_q), .reset(button_1_out));  // open: Qn, preset, en
  J_K_Flip_Flop _1 (
    .J(not_5_out), .clk(clock_1_out), .K(_0_q), .Q(_1_q), .Qn(_1_qn), .reset(button_1_out));  // open: preset, en
  J_K_Flip_Flop _0 (
    .J(nand_6_out), .clk(clock_1_out), .K(nand_8_out), .Q(_0_q), .reset(button_1_out));  // open: Qn, preset, en
  nand nand_2 (nand_2_out, _1_q, _0_q, in_1);
  not not_4 (not_4_out, nand_2_out);
  nand nand_3 (nand_3_out, not_3_out, _0_q);
  not not_5 (not_5_out, nand_3_out);
  nand nand_4 (nand_4_out, _1_qn, not_3_out);
  nand nand_5 (nand_5_out, _1_q, in_1);
  LED led_1 (.in(not_8_out));
  not not_6 (not_6_out, _1_qn);
  not not_7 (not_7_out, in_1);
  nand nand_6 (nand_6_out, nand_4_out, nand_5_out);
  nand nand_7 (nand_7_out, _2_q, _0_q);
  nand nand_8 (nand_8_out, not_6_out, not_7_out);
  not not_8 (not_8_out, nand_7_out);
endmodule
