// Logisim project 3bit-1z10.circ as structural Verilog: 1 circuit, main circuit main
module main (
  input  x2,
  input  x1,
  input  x0,
  output y0,
  output y1,
  output y2,
  output y3,
  output y4,
  output y5,
  output y6,
  output y7
);

  wire nand_1_out, nand_2_out, nand_3_out, nand_4_out, nand_5_out, nand_6_out, nand_7_out, nand_8_out,
       not_1_out, not_2_out, not_3_out;

  not not_1 (not_1_out, x2);
  not not_2 (not_2_out, x1);
  not not_3 (not_3_out, x0);
  not not_4 (y0, nand_1_out);
  nand nand_1 (nand_1_out, not_1_out, not_2_out, not_3_out);
  not not_5 (y1, nand_2_out);
  nand nand_2 (nand_2_out, not_1_out, not_2_out, x0);
  not not_6 (y2, nand_3_out);
  nand nand_3 (nand_3_out, not_1_out, x1, not_3_out);
  nand nand_4 (nand_4_out, not_1_out, x1, x0);
  not not_7 (y3, nand_4_out);
  not not_8 (y4, nand_5_out);
  nand nand_5 (nand_5_out, x2, not_2_out, not_3_out);
  nand nand_6 (nand_6_out, x2, not_2_out, x0);
  not not_9 (y5, nand_6_out);
  not not_10 (y6, nand_7_out);
  nand nand_7 (nand_7_out, x2, x1, not_3_out);
  nand nand_8 (nand_8_out, x2, x1, x0);
  not not_11 (y7, nand_8_out);
endmodule
