// Logisim project 204.circ as structural Verilog: 1 circuit, main circuit main
module main (
);

  wire and_1_out, and_2_out, and_3_out, or_1_out, or_2_out, or_3_out, read_out, reset_out, s_r_ff_1_q,
       undriven;

  Button reset (.out(reset_out));
  Button read (.out(read_out));
  // OR_Gate or_1 has open pins: out=or_1_out
  // OR_Gate or_2 has open pins: out=or_2_out
  buf or_3 (or_3_out, reset_out);  // OR_Gate
  and and_1 (and_1_out, or_1_out, undriven);
  S_R_Flip_Flop s_r_ff_1 (.S(or_2_out), .R(or_3_out), .Q(s_r_ff_1_q));  // open: clk, Qn, preset, reset, en
  and and_2 (and_2_out, and_1_out, s_r_ff_1_q);
  LED led_1 (.in(and_3_out));
  and and_3 (and_3_out, and_2_out, read_out);
endmodule
