// Logisim project 2224.circ as structural Verilog: 2 circuits, main circuit main
module main (
  input  Q1,
  input  Q0,
  input  Z1,
  input  Z0,
  input  in_5,
  output J1,
  output K1,
  output J0,
  output K0
);

  wire and_2_out, and_3_out, not_1_out, not_2_out, not_3_out, not_4_out, not_5_out, not_6_out;

  not not_1 (not_1_out, Z1);
  and and_1 (J1, Q0, not_1_out, not_2_out);
  not not_2 (not_2_out, Z0);
  not not_3 (not_3_out, Q1);
  and and_2 (and_2_out, not_3_out, Z0);
  not not_4 (not_4_out, Q1);
  and and_3 (and_3_out, not_4_out, Z1);
  not not_5 (not_5_out, Z1);
  and and_4 (K0, not_5_out, not_6_out);
  not not_6 (not_6_out, Z0);
  or or_1 (J0, and_2_out, and_3_out);
endmodule

module jk (
  input  Z1,
  input  Z0
);

  wire and_1_out, and_2_out, and_3_out, and_4_out, button_1_out, j_k_ff_1_qn, j_k_ff_2_q, not_1_out,
       not_2_out, or_1_out, reset_out;

  Button button_1 (.out(button_1_out));
  Button reset (.out(reset_out));
  not not_1 (not_1_out, Z1);
  not not_2 (not_2_out, Z0);
  and and_1 (and_1_out, j_k_ff_2_q, not_1_out, not_2_out);
  and and_2 (and_2_out, j_k_ff_1_qn, Z0);
  and and_3 (and_3_out, j_k_ff_1_qn, Z1);
  and and_4 (and_4_out, not_1_out, not_2_out);
  or or_1 (or_1_out, and_2_out, and_3_out);
  J_K_Flip_Flop j_k_ff_1 (
    .J(and_1_out), .clk(button_1_out), .K(reset_out), .Qn(j_k_ff_1_qn), .reset(reset_out));  // open: Q, preset, en
  J_K_Flip_Flop j_k_ff_2 (
    .J(or_1_out), .clk(button_1_out), .K(and_4_out), .Q(j_k_ff_2_q), .reset(reset_out));  // open: Qn, preset, en
endmodule
