// Logisim project 123.circ as structural Verilog: 1 circuit, main circuit main
module main (
  input  z0,
  input  z1
);

  wire j_k_ff_1_q, j_k_ff_1_qn, j_k_ff_2_q, j_k_ff_2_qn, j_k_ff_3_q, j_k_ff_3_qn, nand_1_out, nand_2_out,
       nand_3_out, nand_4_out, nand_5_out, nand_6_out, nand_7_out, nand_8_out, nand_9_out, nand_10_out,
       nand_11_out, nand_12_out, nand_13_out, nand_14_out, nand_15_out, nand_16_out, nand_17_out,
       nand_18_out, nand_19_out, not_1_out, not_2_out, not_3_out, not_4_out, not_5_out, pulse_out, reset_out;

  Button reset (.out(reset_out));
  Button pulse (.out(pulse_out));
  not not_1 (not_1_out, z0);
  not not_2 (not_2_out, z1);
  nand nand_1 (nand_1_out, j_k_ff_1_qn, not_2_out, not_1_out);
  nand nand_2 (nand_2_out, j_k_ff_1_qn, j_k_ff_3_q, not_1_out);
  nand nand_3 (nand_3_out, j_k_ff_2_q, j_k_ff_1_qn, j_k_ff_3_q, not_2_out);
  nand nand_4 (nand_4_out, j_k_ff_2_qn, j_k_ff_3_qn, not_2_out, not_1_out);
  nand nand_5 (nand_5_out, j_k_ff_1_qn, j_k_ff_3_qn, z1, not_1_out);
  nand nand_6 (nand_6_out, j_k_ff_1_qn, j_k_ff_3_q, not_2_out, z0);
  not not_3 (not_3_out, nand_7_out);
  nand nand_7 (nand_7_out, j_k_ff_1_q, j_k_ff_3_qn, j_k_ff_2_qn, not_2_out);
  nand nand_8 (nand_8_out, j_k_ff_1_qn, not_2_out);
  nand nand_9 (nand_9_out, j_k_ff_3_q, j_k_ff_1_qn, not_1_out);
  nand nand_10 (nand_10_out, j_k_ff_1_qn, not_2_out);
  nand nand_11 (nand_11_out, j_k_ff_1_qn, not_1_out);
  nand nand_12 (nand_12_out, z0, j_k_ff_2_qn, not_2_out);
  nand nand_13 (nand_13_out, not_1_out, z1, j_k_ff_2_qn);
  nand nand_14 (nand_14_out, not_2_out, j_k_ff_2_qn, j_k_ff_1_qn);
  not not_4 (not_4_out, nand_4_out);
  nand nand_15 (nand_15_out, not_3_out, not_1_out);
  nand nand_16 (nand_16_out, nand_8_out, nand_9_out);
  not not_5 (not_5_out, nand_14_out);
  LED led_1 (.in(j_k_ff_1_q));
  nand nand_17 (nand_17_out, nand_1_out, nand_2_out, nand_3_out);
  nand nand_18 (nand_18_out, nand_5_out, nand_6_out, nand_15_out);
  nand nand_19 (nand_19_out, nand_10_out, nand_11_out, nand_12_out, nand_13_out);
  LED led_2 (.in(j_k_ff_2_q));
  LED led_3 (.in(j_k_ff_3_q));
  J_K_Flip_Flop j_k_ff_1 (
    .J(nand_17_out), .clk(pulse_out), .K(not_4_out), .Q(j_k_ff_1_q), .Qn(j_k_ff_1_qn), .reset(reset_out));  // open: preset, en
  J_K_Flip_Flop j_k_ff_2 (
    .J(nand_18_out), .clk(pulse_out), .K(nand_16_out), .Q(j_k_ff_2_q), .Qn(j_k_ff_2_qn), .reset(reset_out));  // open: preset, en
  J_K_Flip_Flop j_k_ff_3 (
    .J(nand_19_out), .clk(pulse_out), .K(not_5_out), .Q(j_k_ff_3_q), .Qn(j_k_ff_3_qn), .reset(reset_out));  // open: preset, en

  // Notes on the sheet:
  //   Y0 = -Q2 Q1 Q0    |     Y1 = Q2 -Q1 Q0
  //   -Q2 -Z0
  //   Q0 -Q2 -Z0
  //   -Q2 -Z1
  //   -Q2 -Z0
  //   Z1 -Q1 -Z0
  //   -Q2 -Z1 -Z0
  //   -Q2 Q0 -Z0
  //   Q1 -Q2 Q0 -Z1
  //   -Q1 -Q0 -Z1 -Z0
  //   -Q2 -Q0 Z1 -Z0
  //   -Q2 Q0 -Z1 Z0
  //   Q2 -Q1 -Q0 -Z1
  //   -Z0
endmodule
