// Logisim project regex.circ as structural Verilog: 2 circuits, main circuit main
module main (
  input  Q2,
  input  Q1,
  input  Q0,
  input  Z1,
  input  Z0,
  output J2,
  output K2,
  output J1,
  output K1,
  output J0,
  output K0
);

  wire and_1_out, and_2_out, and_3_out, and_5_out, and_6_out, and_7_out, and_8_out, not_1_out, not_2_out,
       not_3_out, not_4_out, not_5_out, not_6_out, not_7_out, not_8_out, not_9_out, not_10_out, not_11_out,
       not_12_out, not_13_out, not_14_out, not_15_out, not_16_out, not_17_out, not_18_out, not_19_out;

  not not_1 (not_1_out, Z1);
  not not_2 (not_2_out, Z0);
  not not_3 (not_3_out, Z0);
  not not_4 (not_4_out, Q0);
  not not_5 (not_5_out, Z1);
  not not_6 (not_6_out, Z0);
  not not_7 (not_7_out, Q2);
  not not_8 (not_8_out, Q0);
  not not_9 (not_9_out, Q2);
  not not_10 (not_10_out, Q0);
  not not_11 (not_11_out, Z1);
  not not_12 (not_12_out, Z0);
  not not_13 (not_13_out, Q2);
  not not_14 (not_14_out, Z0);
  not not_15 (not_15_out, Q2);
  not not_16 (not_16_out, Q2);
  not not_17 (not_17_out, Q1);
  not not_18 (not_18_out, Z1);
  and and_1 (and_1_out, not_1_out, not_2_out);
  and and_2 (and_2_out, Q0, not_3_out);
  and and_3 (and_3_out, Q1, Q0);
  and and_4 (K2, not_4_out, not_5_out, not_6_out);
  and and_5 (and_5_out, not_7_out, not_8_out, Z1);
  and and_6 (and_6_out, not_9_out, Q0, Z0);
  and and_7 (and_7_out, Q2, not_10_out, not_11_out, not_12_out);
  not not_19 (not_19_out, Z1);
  and and_8 (and_8_out, not_13_out, Q1, Q0, not_14_out);
  or or_1 (J0, not_15_out, Z0, Z1);
  and and_9 (K0, not_16_out, not_17_out, not_18_out);
  or or_2 (J2, and_1_out, and_2_out, and_3_out);
  or or_3 (J1, and_5_out, and_6_out, and_7_out);
  or or_4 (K1, not_19_out, and_8_out);
endmodule

module jk (
  input  Z1,
  input  Z1_2,
  input  Z0,
  input  Z0_2
);

  wire and_1_out, and_2_out, and_3_out, and_4_out, and_5_out, and_6_out, and_7_out, and_8_out, and_9_out,
       and_10_out, and_11_out, and_12_out, and_13_out, and_14_out, and_15_out, and_16_out, and_17_out,
       button_1_out, button_2_out, j_k_ff_1_q, j_k_ff_2_q, j_k_ff_3_q, j_k_ff_4_q, j_k_ff_5_q, j_k_ff_6_q,
       not_1_out, not_2_out, not_3_out, not_4_out, not_5_out, not_6_out, not_7_out, not_8_out, not_9_out,
       not_10_out, not_11_out, not_12_out, not_13_out, not_14_out, not_15_out, not_16_out, not_17_out,
       not_18_out, not_19_out, not_20_out, not_21_out, not_22_out, not_23_out, not_24_out, not_25_out,
       not_26_out, not_27_out, not_28_out, not_29_out, not_30_out, not_31_out, not_32_out, not_33_out,
       not_34_out, not_35_out, not_36_out, or_1_out, or_2_out, or_3_out, or_4_out, or_5_out, or_6_out,
       or_7_out, reset_2_out, reset_out;

  Button button_1 (.out(button_1_out));
  Button reset (.out(reset_out));
  not not_1 (not_1_out, Z1);
  not not_2 (not_2_out, Z0);
  not not_3 (not_3_out, Z0);
  not not_4 (not_4_out, j_k_ff_3_q);
  not not_5 (not_5_out, Z1);
  not not_6 (not_6_out, Z0);
  not not_7 (not_7_out, j_k_ff_1_q);
  not not_8 (not_8_out, j_k_ff_3_q);
  not not_9 (not_9_out, j_k_ff_1_q);
  not not_10 (not_10_out, j_k_ff_3_q);
  not not_11 (not_11_out, Z1);
  not not_12 (not_12_out, Z0);
  not not_13 (not_13_out, Z1);
  not not_14 (not_14_out, j_k_ff_1_q);
  not not_15 (not_15_out, j_k_ff_1_q);
  not not_16 (not_16_out, j_k_ff_2_q);
  not not_17 (not_17_out, Z1);
  and and_1 (and_1_out, not_1_out, not_2_out);
  and and_2 (and_2_out, j_k_ff_3_q, not_3_out);
  and and_3 (and_3_out, j_k_ff_2_q, j_k_ff_3_q);
  and and_4 (and_4_out, not_4_out, not_5_out, not_6_out);
  and and_5 (and_5_out, not_7_out, not_8_out, Z1);
  and and_6 (and_6_out, not_9_out, j_k_ff_3_q, Z0);
  and and_7 (and_7_out, j_k_ff_1_q, not_10_out, not_11_out, not_12_out);
  or or_1 (or_1_out, not_14_out, Z0, Z1);
  and and_8 (and_8_out, not_15_out, not_16_out, not_17_out);
  or or_2 (or_2_out, and_1_out, and_2_out, and_3_out);
  or or_3 (or_3_out, and_5_out, and_6_out, and_7_out);
  J_K_Flip_Flop j_k_ff_1 (
    .J(or_2_out), .clk(button_1_out), .K(and_4_out), .Q(j_k_ff_1_q), .reset(reset_out));  // open: Qn, preset, en
  J_K_Flip_Flop j_k_ff_2 (
    .J(or_3_out), .clk(button_1_out), .K(not_13_out), .Q(j_k_ff_2_q), .reset(reset_out));  // open: Qn, preset, en
  J_K_Flip_Flop j_k_ff_3 (
    .J(or_1_out), .clk(button_1_out), .K(and_8_out), .Q(j_k_ff_3_q), .reset(reset_out));  // open: Qn, preset, en
  LED led_1 (.in(j_k_ff_1_q));
  Button button_2 (.out(button_2_out));
  Button reset_2 (.out(reset_2_out));
  LED led_2 (.in(j_k_ff_2_q));
  LED led_3 (.in(j_k_ff_3_q));
  not not_18 (not_18_out, Z1_2);
  not not_19 (not_19_out, Z0_2);
  not not_20 (not_20_out, Z0_2);
  not not_21 (not_21_out, j_k_ff_6_q);
  not not_22 (not_22_out, Z1_2);
  not not_23 (not_23_out, Z0_2);
  not not_24 (not_24_out, j_k_ff_4_q);
  not not_25 (not_25_out, j_k_ff_6_q);
  not not_26 (not_26_out, j_k_ff_4_q);
  not not_27 (not_27_out, j_k_ff_6_q);
  not not_28 (not_28_out, Z1_2);
  not not_29 (not_29_out, Z0_2);
  not not_30 (not_30_out, j_k_ff_4_q);
  not not_31 (not_31_out, Z0_2);
  not not_32 (not_32_out, j_k_ff_4_q);
  not not_33 (not_33_out, j_k_ff_4_q);
  not not_34 (not_34_out, j_k_ff_5_q);
  not not_35 (not_35_out, Z1_2);
  and and_9 (and_9_out, not_18_out, not_19_out);
  and and_10 (and_10_out, j_k_ff_6_q, not_20_out);
  and and_11 (and_11_out, j_k_ff_5_q, j_k_ff_6_q);
  and and_12 (and_12_out, not_21_out, not_22_out, not_23_out);
  and and_13 (and_13_out, not_24_out, not_25_out, Z1_2);
  and and_14 (and_14_out, not_26_out, j_k_ff_6_q, Z0_2);
  and and_15 (and_15_out, j_k_ff_4_q, not_27_out, not_28_out, not_29_out);
  not not_36 (not_36_out, Z1_2);
  and and_16 (and_16_out, not_30_out, j_k_ff_5_q, j_k_ff_6_q, not_31_out);
  or or_4 (or_4_out, not_32_out, Z0_2, Z1_2);
  and and_17 (and_17_out, not_33_out, not_34_out, not_35_out);
  or or_5 (or_5_out, and_9_out, and_10_out, and_11_out);
  or or_6 (or_6_out, and_13_out, and_14_out, and_15_out);
  or or_7 (or_7_out, not_36_out, and_16_out);
  J_K_Flip_Flop j_k_ff_4 (
    .J(or_5_out), .clk(button_2_out), .K(and_12_out), .Q(j_k_ff_4_q), .reset(reset_2_out));  // open: Qn, preset, en
  J_K_Flip_Flop j_k_ff_5 (
    .J(or_6_out), .clk(button_2_out), .K(or_7_out), .Q(j_k_ff_5_q), .reset(reset_2_out));  // open: Qn, preset, en
  J_K_Flip_Flop j_k_ff_6 (
    .J(or_4_out), .clk(button_2_out), .K(and_17_out), .Q(j_k_ff_6_q), .reset(reset_2_out));  // open: Qn, preset, en
  LED led_4 (.in(j_k_ff_4_q));
  LED led_5 (.in(j_k_ff_5_q));
  LED led_6 (.in(j_k_ff_6_q));
endmodule
