// Logisim project xx.circ as structural Verilog: 1 circuit, main circuit main
module main (
);

  wire nand_1_out, nand_2_out, nand_3_out, nand_4_out, nand_5_out, nand_6_out, nand_7_out, nand_8_out,
       nand_9_out, nand_10_out, nand_11_out, not_1_out, not_2_out, not_3_out, not_4_out, not_5_out,
       not_6_out, Q0_q, Q0_qn, Q1_q, Q1_qn, Q2_q, Q2_qn, z0_out, z1_out;

  Button z1 (.out(z1_out));
  Button z0 (.out(z0_out));
  not not_1 (not_1_out, z1_out);
  not not_2 (not_2_out, z0_out);
  nand nand_1 (nand_1_out, Q1_qn, not_1_out);
  nand nand_2 (nand_2_out, nand_1_out, not_2_out);
  not not_3 (not_3_out, nand_3_out);
  nand nand_3 (nand_3_out, Q1_q, z1_out, not_2_out);
  nand nand_4 (nand_4_out, not_2_out, nand_5_out);
  nand nand_5 (nand_5_out, Q0_qn, z1_out);
  nand nand_6 (nand_6_out, Q0_q, not_1_out, not_2_out);
  nand nand_7 (nand_7_out, not_2_out, nand_8_out);
  nand nand_8 (nand_8_out, Q2_q, not_1_out);
  nand nand_9 (nand_9_out, not_2_out, z1_out, Q2_qn);
  not not_4 (not_4_out, nand_6_out);
  not not_5 (not_5_out, nand_9_out);
  J_K_Flip_Flop Q2 (.Q(Q2_q), .Qn(Q2_qn), .preset(not_3_out), .reset(nand_2_out));  // open: J, clk, K, en
  J_K_Flip_Flop Q1 (.Q(Q1_q), .Qn(Q1_qn), .preset(not_4_out), .reset(nand_4_out));  // open: J, clk, K, en
  J_K_Flip_Flop Q0 (.Q(Q0_q), .Qn(Q0_qn), .preset(not_5_out), .reset(nand_7_out));  // open: J, clk, K, en
  nand nand_10 (nand_10_out, Q2_q, Q1_q);
  nand nand_11 (nand_11_out, Q1_qn, Q0_qn);
  not not_6 (not_6_out, nand_10_out);
  LED Y1 (.in(not_6_out));
  LED Y0 (.in(nand_11_out));
endmodule
