// Logisim project aaa.circ as structural Verilog: 1 circuit, main circuit main
module main (
  output out_1
);

  wire _0_out, _1_out, _2_out, nand_1_out, nand_2_out, nand_3_out, nand_4_out, nand_5_out, nand_6_out,
       nand_7_out, nand_8_out, nand_9_out, nand_10_out, nand_11_out, nand_12_out, nand_13_out, nand_14_out,
       nand_15_out, not_1_out, not_2_out, not_3_out, not_4_out, not_5_out, not_6_out, not_7_out, not_8_out,
       not_9_out, not_10_out, not_11_out, read_out, reset_out, s_r_ff_1_q, s_r_ff_2_q, s_r_ff_2_qn, start_out;

  Button start (.out(start_out));
  Button _0 (.out(_0_out));
  Button _1 (.out(_1_out));
  Button _2 (.out(_2_out));
  Button reset (.out(reset_out));
  Button read (.out(read_out));
  not not_1 (not_1_out, _1_out);
  not not_2 (not_2_out, _2_out);
  not not_3 (not_3_out, reset_out);
  nand nand_1 (nand_1_out, not_1_out, not_2_out);
  not not_4 (not_4_out, start_out);
  nand nand_2 (nand_2_out, s_r_ff_1_q, _0_out);
  not not_5 (not_5_out, nand_1_out);
  not not_6 (not_6_out, read_out);
  nand nand_3 (nand_3_out, not_4_out, nand_2_out);
  nand nand_4 (nand_4_out, not_3_out, s_r_ff_2_qn);
  nand nand_5 (nand_5_out, not_1_out, not_2_out);
  nand nand_6 (nand_6_out, not_5_out, not_6_out);
  S_R_Flip_Flop s_r_ff_1 (.Q(s_r_ff_1_q), .preset(nand_3_out), .reset(nand_4_out));  // open: S, clk, R, Qn, en
  nand nand_7 (nand_7_out, 1'b1, nand_6_out);
  not not_7 (not_7_out, nand_7_out);
  not not_8 (not_8_out, _0_out);
  not not_9 (not_9_out, read_out);
  nand nand_8 (nand_8_out, not_7_out, s_r_ff_1_q);
  nand nand_9 (nand_9_out, not_8_out, not_3_out);
  nand nand_10 (nand_10_out, not_9_out, not_2_out);
  nand nand_11 (nand_11_out, s_r_ff_2_q, nand_5_out);
  nand nand_12 (nand_12_out, nand_11_out, nand_8_out);
  nand nand_13 (nand_13_out, nand_10_out, 1'b1);
  S_R_Flip_Flop s_r_ff_2 (
    .Q(s_r_ff_2_q), .Qn(s_r_ff_2_qn), .preset(nand_12_out), .reset(nand_9_out));  // open: S, clk, R, en
  not not_10 (not_10_out, nand_13_out);
  not not_11 (not_11_out, nand_14_out);
  nand nand_14 (nand_14_out, not_10_out, s_r_ff_2_q);
  nand nand_15 (nand_15_out, not_11_out, read_out);
  not not_12 (out_1, nand_15_out);
endmodule
