// Logisim project asyncautomat.circ as structural Verilog: 2 circuits, main circuit main
module main (
);

  wire and_1_out, and_2_out, not_1_out, not_2_out, not_3_out, not_4_out, not_5_out, or_1_out, or_2_out,
       or_3_out, or_4_out, or_5_out, or_6_out, or_7_out, or_8_out, or_9_out, or_10_out, or_11_out, or_12_out,
       Q0_out, Q1_out, Q2_out, z0_out, z1_out;

  Button z1 (.out(z1_out));
  Button z0 (.out(z0_out));
  not not_1 (not_1_out, z1_out);
  not not_2 (not_2_out, z0_out);
  or or_1 (or_1_out, z1_out, Q1_out);
  or or_2 (or_2_out, Q2_out, z1_out);
  or or_3 (or_3_out, Q1_out, Q2_out);
  or or_4 (or_4_out, not_1_out, Q0_out, not_3_out);
  or or_5 (or_5_out, Q1_out, not_1_out);
  or or_6 (or_6_out, Q0_out, Q1_out);
  or or_7 (or_7_out, z1_out, Q0_out, Q1_out);
  or or_8 (or_8_out, not_4_out, Q1_out);
  or or_9 (or_9_out, not_3_out, Q0_out);
  or or_10 (or_10_out, not_4_out, z1_out);
  not not_3 (not_3_out, Q1_out);
  not not_4 (not_4_out, Q2_out);
  and Q2 (Q2_out, or_1_out, or_2_out, or_3_out, not_2_out);
  and Q1 (Q1_out, or_4_out, or_5_out, or_6_out, not_2_out);
  and Q0 (Q0_out, or_7_out, or_8_out, or_10_out, or_9_out, not_2_out);
  not not_5 (not_5_out, Q2_out);
  and and_1 (and_1_out, Q2_out, Q1_out);
  or or_11 (or_11_out, Q2_out, Q0_out);
  or or_12 (or_12_out, not_5_out, Q1_out);
  LED Y1 (.in(and_1_out));
  LED Y0 (.in(and_2_out));
  and and_2 (and_2_out, or_11_out, or_12_out);
endmodule

module test (
);

  wire nor_1_out, nor_2_out, nor_3_out, nor_4_out, nor_5_out, nor_6_out, nor_7_out, nor_8_out, nor_9_out,
       nor_10_out, nor_11_out, nor_12_out, nor_13_out, nor_14_out, nor_15_out, nor_16_out, not_1_out,
       not_2_out, not_3_out, not_4_out, not_5_out, not_6_out, not_7_out, z0_out, z1_out;

  Button z1 (.out(z1_out));
  Button z0 (.out(z0_out));
  not not_1 (not_1_out, z1_out);
  nor nor_1 (nor_1_out, nor_14_out, nor_12_out);
  nor nor_2 (nor_2_out, not_5_out, nor_14_out);
  not not_2 (not_2_out, nor_2_out);
  not not_3 (not_3_out, nor_1_out);
  nor nor_3 (nor_3_out, not_4_out, nor_12_out);
  nor nor_4 (nor_4_out, not_4_out, z1_out);
  nor nor_5 (nor_5_out, z1_out, nor_12_out);
  nor nor_6 (nor_6_out, nor_11_out, z1_out);
  nor nor_7 (nor_7_out, nor_12_out, nor_11_out);
  nor nor_8 (nor_8_out, not_1_out, not_2_out);
  nor nor_9 (nor_9_out, nor_12_out, not_1_out);
  nor nor_10 (nor_10_out, not_3_out, z1_out);
  not not_4 (not_4_out, nor_11_out);
  nor nor_11 (nor_11_out, nor_5_out, nor_6_out, nor_7_out, z0_out);
  not not_5 (not_5_out, nor_12_out);
  nor nor_12 (nor_12_out, nor_8_out, nor_9_out, nor_1_out, z0_out);
  nor nor_13 (nor_13_out, z0_out, nor_10_out, nor_3_out, nor_2_out);
  not not_6 (not_6_out, nor_13_out);
  LED Q2 (.in(nor_11_out));
  nor nor_14 (nor_14_out, not_6_out, nor_4_out);
  LED Q0 (.in(nor_14_out));
  LED Q1 (.in(nor_12_out));
  nor nor_15 (nor_15_out, not_4_out, not_5_out);
  LED Y1 (.in(nor_15_out));
  not not_7 (not_7_out, nor_16_out);
  nor nor_16 (nor_16_out, nor_12_out, nor_14_out);
  LED Y0 (.in(not_7_out));

  // Notes on the sheet:
  //   Q1+Q0 = A
  //   ~Q1+Q0=B
  //   ~Q2+Q1
  //   ~Q2+Z1
  //   Z1+Q1
  //   Q2+Z1
  //   Q2+Q1
  //   ~B+~Z1
  //   Q1+~Z1
  //   ~A+Z1
endmodule
