// Logisim project demultiplekser2bitNOR.circ as structural Verilog: 1 circuit, main circuit main
module main (
  input  X,
  input  B,
  input  A,
  output Y0,
  output Y1,
  output Y2,
  output Y3
);

  wire nor_1_out, nor_2_out, nor_3_out, nor_4_out, nor_5_out, nor_6_out, nor_7_out, nor_8_out, nor_9_out,
       nor_10_out, nor_11_out, nor_13_out, nor_15_out, nor_17_out;

  nor nor_1 (nor_1_out, B, B);
  nor nor_2 (nor_2_out, A, A);
  nor nor_3 (nor_3_out, B, A);
  nor nor_4 (nor_4_out, nor_11_out, X);
  nor nor_5 (nor_5_out, B, nor_2_out);
  nor nor_6 (nor_6_out, nor_13_out, X);
  nor nor_7 (nor_7_out, A, nor_1_out);
  nor nor_8 (nor_8_out, nor_15_out, X);
  nor nor_9 (nor_9_out, nor_1_out, nor_2_out);
  nor nor_10 (nor_10_out, nor_17_out, X);
  nor nor_11 (nor_11_out, nor_3_out, nor_3_out);
  nor nor_12 (Y0, nor_4_out, nor_4_out);
  nor nor_13 (nor_13_out, nor_5_out, nor_5_out);
  nor nor_14 (Y1, nor_6_out, nor_6_out);
  nor nor_15 (nor_15_out, nor_7_out, nor_7_out);
  nor nor_16 (Y2, nor_8_out, nor_8_out);
  nor nor_17 (nor_17_out, nor_9_out, nor_9_out);
  nor nor_18 (Y3, nor_10_out, nor_10_out);
endmodule
