// Logisim project detektor_liczby.circ as structural Verilog: 6 circuits, main circuit main
module main (
  input  Z1,
  input  Z0,
  output J2,
  output K2,
  output J1,
  output Y1,
  output K1,
  output Y0,
  output J0,
  output K0
);

  wire _0_q, _1_q, _2_q, clock_1_out, nand_1_out, nand_2_out, nand_3_out, nand_4_out, nand_5_out, nand_6_out,
       nand_7_out, nand_8_out, nand_9_out, nand_10_out, nand_11_out, nand_12_out, nand_13_out, nand_15_out,
       nand_16_out, nand_17_out, nand_19_out, nand_20_out, nand_21_out, nand_22_out, nand_23_out,
       nand_24_out, nand_25_out, nand_26_out, nand_27_out, nand_28_out, nand_29_out, nand_30_out,
       nand_31_out, nand_34_out, nand_35_out, nand_37_out, nand_38_out, nand_40_out, nand_41_out,
       nand_42_out, nand_43_out, nand_44_out, nand_46_out, nand_47_out;

  nand nand_1 (nand_1_out, _0_q, _0_q);
  nand nand_2 (nand_2_out, Z1, Z1);
  nand nand_3 (nand_3_out, Z0, Z0);
  nand nand_4 (nand_4_out, Z1, Z1);
  nand nand_5 (nand_5_out, _2_q, _2_q);
  nand nand_6 (nand_6_out, _0_q, _0_q);
  nand nand_7 (nand_7_out, Z0, Z0);
  nand nand_8 (nand_8_out, _1_q, _1_q);
  nand nand_9 (nand_9_out, _1_q, Z0);
  nand nand_10 (nand_10_out, _2_q, Z0);
  nand nand_11 (nand_11_out, _1_q, nand_1_out);
  nand nand_12 (nand_12_out, nand_2_out, nand_3_out);
  nand nand_13 (nand_13_out, _1_q, _0_q);
  nand nand_14 (K2, _0_q, nand_4_out);
  nand nand_15 (nand_15_out, nand_5_out, nand_6_out);
  nand nand_16 (nand_16_out, _0_q, nand_7_out);
  nand nand_17 (nand_17_out, Z1, nand_8_out);
  nand nand_18 (K0, nand_9_out, nand_10_out);
  nand nand_19 (nand_19_out, nand_11_out, nand_11_out);
  nand nand_20 (nand_20_out, nand_12_out, nand_12_out);
  nand nand_21 (nand_21_out, nand_13_out, nand_13_out);
  nand nand_22 (nand_22_out, nand_15_out, nand_15_out);
  nand nand_23 (nand_23_out, Z0, Z0);
  nand nand_24 (nand_24_out, nand_16_out, nand_16_out);
  nand nand_25 (nand_25_out, Z1, Z1);
  nand nand_26 (nand_26_out, nand_17_out, nand_17_out);
  nand nand_27 (nand_27_out, _2_q, _2_q);
  nand nand_28 (nand_28_out, nand_19_out, nand_20_out);
  nand nand_29 (nand_29_out, nand_21_out, Z0);
  nand nand_30 (nand_30_out, _1_q, _0_q);
  nand nand_31 (nand_31_out, nand_22_out, nand_23_out);
  nand nand_32 (K1, nand_24_out, nand_25_out);
  nand nand_33 (J0, nand_26_out, nand_27_out);
  nand nand_34 (nand_34_out, nand_28_out, nand_29_out);
  nand nand_35 (nand_35_out, nand_30_out, nand_30_out);
  nand nand_36 (J1, nand_31_out, nand_31_out);
  Clock clock_1 (.out(clock_1_out));
  nand nand_37 (nand_37_out, nand_34_out, nand_34_out);
  nand nand_38 (nand_38_out, nand_35_out, Z1);
  nand nand_39 (J2, nand_37_out, nand_38_out);
  J_K_Flip_Flop _2 (.J(J2), .clk(clock_1_out), .K(K2), .Q(_2_q));  // open: Qn, preset, en, reset
  J_K_Flip_Flop _1 (.J(J1), .clk(clock_1_out), .K(K1), .Q(_1_q));  // open: Qn, preset, en, reset
  J_K_Flip_Flop _0 (.J(J0), .clk(clock_1_out), .K(K0), .Q(_0_q));  // open: Qn, preset, en, reset
  nand nand_40 (nand_40_out, _2_q, _2_q);
  nand nand_41 (nand_41_out, _1_q, _1_q);
  nand nand_42 (nand_42_out, _1_q, _0_q);
  nand nand_43 (nand_43_out, _2_q, _2_q);
  nand nand_44 (nand_44_out, nand_40_out, nand_41_out);
  nand nand_45 (Y0, nand_42_out, nand_43_out);
  nand nand_46 (nand_46_out, nand_44_out, nand_44_out);
  nand nand_47 (nand_47_out, nand_46_out, _0_q);
  nand nand_48 (Y1, nand_47_out, nand_47_out);
endmodule

module Y (
  input  Q2,
  input  Q1,
  input  Q0,
  output Y1,
  output Y0
);

  wire nand_1_out, nand_2_out, nand_3_out, nand_4_out, nand_5_out, nand_7_out, nand_8_out;

  nand nand_1 (nand_1_out, Q2, Q2);
  nand nand_2 (nand_2_out, Q1, Q1);
  nand nand_3 (nand_3_out, Q1, Q0);
  nand nand_4 (nand_4_out, Q2, Q2);
  nand nand_5 (nand_5_out, nand_1_out, nand_2_out);
  nand nand_6 (Y0, nand_3_out, nand_4_out);
  nand nand_7 (nand_7_out, nand_5_out, nand_5_out);
  nand nand_8 (nand_8_out, nand_7_out, Q0);
  nand nand_9 (Y1, nand_8_out, nand_8_out);
endmodule

module mini (
  input  Z1,
  input  Z0,
  output Y1,
  output Y0,
  output Y1_2,
  output Y0_2
);

  wire _0_q, _0_qn, _1_q, _1_qn, _2_q, _2_qn, and_1_out, and_2_out, and_3_out, and_4_out, and_5_out,
       and_6_out, and_7_out, and_8_out, and_10_out, clock_1_out, not_1_out, not_2_out, or_1_out, or_2_out,
       or_3_out, or_4_out, or_5_out, or_6_out, or_7_out;

  not not_1 (not_1_out, Z1);
  not not_2 (not_2_out, Z0);
  or or_1 (or_1_out, Z1, Z0);
  and and_1 (and_1_out, not_1_out, not_2_out);
  and and_2 (and_2_out, _0_q, or_1_out);
  and and_3 (and_3_out, _0_qn, and_1_out);
  or or_2 (or_2_out, _2_q, _1_q);
  or or_3 (or_3_out, and_2_out, and_3_out);
  and and_4 (and_4_out, _2_qn, _0_qn);
  and and_5 (and_5_out, and_4_out, not_2_out);
  or or_4 (or_4_out, _0_qn, or_5_out);
  or or_5 (or_5_out, Z1, Z0);
  and and_6 (and_6_out, _1_q, or_3_out);
  or or_6 (or_6_out, _0_qn, Z1);
  J_K_Flip_Flop _0 (.J(or_7_out), .clk(clock_1_out), .K(and_7_out), .Q(_0_q), .Qn(_0_qn));  // open: preset, en, reset
  or or_7 (or_7_out, or_2_out, not_1_out);
  and and_7 (and_7_out, or_2_out, Z0);
  J_K_Flip_Flop _1 (.J(and_5_out), .clk(clock_1_out), .K(or_4_out), .Q(_1_q), .Qn(_1_qn));  // open: preset, en, reset
  J_K_Flip_Flop _2 (.J(and_6_out), .clk(clock_1_out), .K(or_6_out), .Q(_2_q), .Qn(_2_qn));  // open: preset, en, reset
  Clock clock_1 (.out(clock_1_out));
  and and_8 (and_8_out, _0_q, _1_qn);
  and and_9 (Y1, and_8_out, _2_qn);
  and and_10 (and_10_out, _0_q, _1_q);
  or or_8 (Y0, and_10_out, _2_q);
endmodule

module mini_nand (
  input  Z1,
  input  Z0,
  output Y1,
  output Y0,
  output Y1_2,
  output Y0_2
);

  wire _0_q, _0_qn, _1_q, _1_qn, _2_qn, clock_1_out, nand_1_out, nand_2_out, nand_3_out, nand_4_out,
       nand_5_out, nand_6_out, nand_7_out, nand_8_out, nand_9_out, nand_10_out, nand_11_out, nand_12_out,
       nand_13_out, nand_14_out, nand_15_out, nand_16_out, nand_17_out, not_1_out, not_2_out, not_3_out,
       not_4_out, not_5_out, not_6_out, not_7_out, not_8_out, not_9_out, not_10_out;

  not not_1 (not_1_out, Z1);
  not not_2 (not_2_out, Z0);
  nand nand_1 (nand_1_out, not_2_out, not_1_out);
  not not_3 (not_3_out, nand_2_out);
  nand nand_2 (nand_2_out, not_1_out, not_2_out);
  nand nand_3 (nand_3_out, _0_q, nand_1_out);
  nand nand_4 (nand_4_out, _0_qn, not_3_out);
  nand nand_5 (nand_5_out, _2_qn, _0_qn);
  nand nand_6 (nand_6_out, not_1_out, not_2_out);
  not not_4 (not_4_out, nand_6_out);
  nand nand_7 (nand_7_out, nand_3_out, nand_4_out);
  nand nand_8 (nand_8_out, _2_qn, _1_qn);
  not not_5 (not_5_out, nand_8_out);
  nand nand_9 (nand_9_out, nand_8_out, Z0);
  not not_6 (not_6_out, nand_5_out);
  nand nand_10 (nand_10_out, not_6_out, not_2_out);
  nand nand_11 (nand_11_out, _0_q, not_4_out);
  nand nand_12 (nand_12_out, _1_q, nand_7_out);
  nand nand_13 (nand_13_out, _0_q, not_1_out);
  nand nand_14 (nand_14_out, not_5_out, Z1);
  not not_7 (not_7_out, nand_9_out);
  not not_8 (not_8_out, nand_10_out);
  not not_9 (not_9_out, nand_12_out);
  Clock clock_1 (.out(clock_1_out));
  J_K_Flip_Flop _0 (
    .J(nand_14_out), .clk(clock_1_out), .K(not_7_out), .Q(_0_q), .Qn(_0_qn));  // open: preset, en, reset
  J_K_Flip_Flop _1 (
    .J(not_8_out), .clk(clock_1_out), .K(nand_11_out), .Q(_1_q), .Qn(_1_qn));  // open: preset, en, reset
  J_K_Flip_Flop _2 (.J(not_9_out), .clk(clock_1_out), .K(nand_13_out), .Qn(_2_qn));  // open: Q, preset, en, reset
  nand nand_15 (nand_15_out, _0_q, _1_qn);
  nand nand_16 (nand_16_out, _0_q, _1_q);
  not not_10 (not_10_out, nand_15_out);
  nand nand_17 (nand_17_out, not_10_out, _2_qn);
  not not_11 (Y1, nand_17_out);
  nand nand_18 (Y0, nand_16_out, _2_qn);
endmodule

module kk (
  input  c,
  input  b,
  input  a,
  output x
);

  wire nand_1_out, nand_2_out, nand_3_out;

  nand nand_1 (nand_1_out, c, c);
  nand nand_2 (nand_2_out, b, b);
  nand nand_3 (nand_3_out, a, a);
  nand nand_4 (x, nand_1_out, nand_2_out, nand_3_out);
endmodule

module mm (
  input  Z1,
  input  Z1_2,
  input  Z0,
  output J2,
  output K2,
  output J1,
  output Y1,
  output K1,
  output Y0,
  output J0,
  output K0
);

  wire _0_q, _1_q, _2_q, clock_1_out, nand_1_out, nand_2_out, nand_3_out, nand_4_out, nand_5_out, nand_6_out,
       nand_7_out, nand_8_out, nand_9_out, nand_10_out, nand_11_out, nand_12_out, nand_13_out, nand_15_out,
       nand_16_out, nand_17_out, nand_19_out, nand_20_out, nand_21_out, nand_22_out, nand_23_out,
       nand_24_out, nand_25_out, nand_26_out, nand_27_out, nand_28_out, nand_29_out, nand_30_out,
       nand_31_out, nand_34_out, nand_35_out, nand_37_out, nand_38_out, nand_40_out, nand_41_out,
       nand_42_out, nand_43_out, nand_44_out, nand_46_out, nand_47_out;

  nand nand_1 (nand_1_out, _0_q, _0_q);
  nand nand_2 (nand_2_out, Z1_2, Z1_2);
  nand nand_3 (nand_3_out, Z0, Z0);
  nand nand_4 (nand_4_out, Z1_2, Z1_2);
  nand nand_5 (nand_5_out, _2_q, _2_q);
  nand nand_6 (nand_6_out, _0_q, _0_q);
  nand nand_7 (nand_7_out, Z0, Z0);
  nand nand_8 (nand_8_out, _1_q, _1_q);
  nand nand_9 (nand_9_out, _1_q, Z0);
  nand nand_10 (nand_10_out, _2_q, Z0);
  nand nand_11 (nand_11_out, _1_q, nand_1_out);
  nand nand_12 (nand_12_out, nand_2_out, nand_3_out);
  nand nand_13 (nand_13_out, _1_q, _0_q);
  nand nand_14 (K2, _0_q, nand_4_out);
  nand nand_15 (nand_15_out, nand_5_out, nand_6_out);
  nand nand_16 (nand_16_out, _0_q, nand_7_out);
  nand nand_17 (nand_17_out, Z1_2, nand_8_out);
  nand nand_18 (K0, nand_9_out, nand_10_out);
  nand nand_19 (nand_19_out, nand_11_out, nand_11_out);
  nand nand_20 (nand_20_out, nand_12_out, nand_12_out);
  nand nand_21 (nand_21_out, nand_13_out, nand_13_out);
  nand nand_22 (nand_22_out, nand_15_out, nand_15_out);
  nand nand_23 (nand_23_out, Z0, Z0);
  nand nand_24 (nand_24_out, nand_16_out, nand_16_out);
  nand nand_25 (nand_25_out, Z1_2, Z1_2);
  nand nand_26 (nand_26_out, nand_17_out, nand_17_out);
  nand nand_27 (nand_27_out, _2_q, _2_q);
  nand nand_28 (nand_28_out, nand_19_out, nand_20_out);
  nand nand_29 (nand_29_out, nand_21_out, Z0);
  nand nand_30 (nand_30_out, _1_q, _0_q);
  nand nand_31 (nand_31_out, nand_22_out, nand_23_out);
  nand nand_32 (K1, nand_24_out, nand_25_out);
  nand nand_33 (J0, nand_26_out, nand_27_out);
  nand nand_34 (nand_34_out, nand_28_out, nand_29_out);
  nand nand_35 (nand_35_out, nand_30_out, nand_30_out);
  nand nand_36 (J1, nand_31_out, nand_31_out);
  Clock clock_1 (.out(clock_1_out));
  nand nand_37 (nand_37_out, nand_34_out, nand_34_out);
  nand nand_38 (nand_38_out, nand_35_out, Z1_2);
  nand nand_39 (J2, nand_37_out, nand_38_out);
  J_K_Flip_Flop _2 (.J(J2), .clk(clock_1_out), .K(K2), .Q(_2_q));  // open: Qn, preset, en, reset
  J_K_Flip_Flop _1 (.J(J1), .clk(clock_1_out), .K(K1), .Q(_1_q));  // open: Qn, preset, en, reset
  J_K_Flip_Flop _0 (.J(J0), .clk(clock_1_out), .K(K0), .Q(_0_q));  // open: Qn, preset, en, reset
  nand nand_40 (nand_40_out, _2_q, _2_q);
  nand nand_41 (nand_41_out, _1_q, _1_q);
  nand nand_42 (nand_42_out, _1_q, _0_q);
  nand nand_43 (nand_43_out, _2_q, _2_q);
  nand nand_44 (nand_44_out, nand_40_out, nand_41_out);
  nand nand_45 (Y0, nand_42_out, nand_43_out);
  nand nand_46 (nand_46_out, nand_44_out, nand_44_out);
  nand nand_47 (nand_47_out, nand_46_out, _0_q);
  nand nand_48 (Y1, nand_47_out, nand_47_out);
endmodule
