// Logisim project flip-flop.circ as structural Verilog: 1 circuit, main circuit main
module main (
  input  in_1,
  input  in_2,
  input  in_3,
  input  in_4,
  input  in_5,
  input  in_6,
  input  in_7,
  output out_8,
  output out_9,
  output out_10,
  output out_11,
  output out_12,
  output Q,
  output out_14,
  output out_15,
  output out_16,
  output out_17,
  output out_18,
  output out_19
);

  wire button_1_out, clock_1_out, clock_2_out, clock_3_out, clock_4_out, not_1_out, not_2_out, R_2_out,
       R_3_out, R_4_out, R_5_out, R_6_out, R_out, S_2_out, S_3_out, S_4_out, S_out;

  Clock clock_1 (.out(clock_1_out));
  Button S (.out(S_out));
  Clock clock_2 (.out(clock_2_out));
  Button button_1 (.out(button_1_out));
  Button S_2 (.out(S_2_out));
  Button R (.out(R_out));
  T_Flip_Flop T (.clk(clock_1_out), .T(in_1), .Q(out_8), .Qn(out_10), .preset(S_out), .reset(R_2_out));  // open: en
  Button R_2 (.out(R_2_out));
  S_R_Flip_Flop RS (
    .S(in_3), .clk(clock_2_out), .R(button_1_out), .Q(out_12), .Qn(out_14), .preset(S_2_out), .reset(R_3_out));  // open: en
  Button R_3 (.out(R_3_out));
  not not_1 (not_1_out, in_6);
  nand nand_1 (out_16, not_1_out, out_18);
  nand nand_2 (out_18, out_16, not_2_out);
  not not_2 (not_2_out, R_out);
  Clock clock_3 (.out(clock_3_out));
  Button S_3 (.out(S_3_out));
  D_Flip_Flop D (.clk(clock_3_out), .D(in_2), .Q(out_9), .Qn(out_11), .preset(S_3_out), .reset(R_4_out));  // open: en
  Button R_4 (.out(R_4_out));
  Button J ();  // open: out
  Button K ();  // open: out
  nor nor_1 (out_17, in_7, out_19);
  nor nor_2 (out_19, out_17, R_5_out);
  Button R_5 (.out(R_5_out));
  Clock clock_4 (.out(clock_4_out));
  Button S_4 (.out(S_4_out));
  J_K_Flip_Flop JK (
    .J(in_4), .clk(clock_4_out), .K(in_5), .Q(Q), .Qn(out_15), .preset(S_4_out), .reset(R_6_out));  // open: en
  Button R_6 (.out(R_6_out));
endmodule
