// Logisim project jk-parametryczny-siatki.circ as structural Verilog: 1 circuit, main circuit main
module main (
  input  b1,
  input  b0,
  input  s1,
  input  s0,
  output j1,
  output k1,
  output j0,
  output k0
);

  wire nand_1_out, nand_2_out, nand_3_out, nand_4_out, nand_5_out, nand_6_out, nand_7_out, nand_8_out,
       nand_9_out, nand_10_out, nand_11_out, nand_12_out, nand_13_out, nand_14_out, nand_15_out, nand_16_out,
       nand_17_out, nand_18_out, nand_19_out, nand_20_out, nand_21_out, nand_22_out;

  nand nand_1 (nand_1_out, b1, b1);
  nand nand_2 (nand_2_out, s1, s1);
  nand nand_3 (nand_3_out, b0, b0);
  nand nand_4 (nand_4_out, s1, s1);
  nand nand_5 (nand_5_out, b0, b0);
  nand nand_6 (nand_6_out, s0, s0);
  nand nand_7 (nand_7_out, b1, b1);
  nand nand_8 (nand_8_out, s1, s1);
  nand nand_9 (nand_9_out, b0, b0);
  nand nand_10 (nand_10_out, s1, s1);
  nand nand_11 (nand_11_out, s0, s0);
  nand nand_12 (nand_12_out, b1, b1);
  nand nand_13 (nand_13_out, s1, s1);
  nand nand_14 (nand_14_out, b1, b1);
  nand nand_15 (nand_15_out, s0, s0);
  nand nand_16 (nand_16_out, nand_1_out, b0, nand_2_out, s0);
  nand nand_17 (nand_17_out, nand_3_out, nand_4_out);
  nand nand_18 (nand_18_out, nand_5_out, nand_6_out);
  nand nand_19 (nand_19_out, nand_7_out, nand_8_out, s0);
  nand nand_20 (nand_20_out, b1, nand_9_out, nand_10_out, nand_11_out);
  nand nand_21 (nand_21_out, nand_12_out, nand_13_out, s0);
  nand nand_22 (nand_22_out, nand_14_out, s1, nand_15_out);
  nand nand_23 (j1, nand_16_out, nand_16_out);
  nand nand_24 (k1, nand_17_out, nand_18_out);
  nand nand_25 (j0, nand_19_out, nand_20_out);
  nand nand_26 (k0, nand_21_out, nand_22_out);
endmodule
