// Logisim project licznik01235467.circ as structural Verilog: 3 circuits, main circuit main
module main (
);

  wire clock_1_out, D0_qn, D1_qn, D2_qn, nand_1_out, nand_2_out, nand_3_out, nand_4_out, nand_5_out,
       nand_6_out, nand_7_out, nand_8_out, nand_9_out, nand_10_out, nand_11_out, nand_12_out, reset_out;
  wire [3:0] D0_q;

  nand nand_1 (nand_1_out, D2_qn, D0_q[1], D0_q[0]);
  nand nand_2 (nand_2_out, D0_q[2], D1_qn);
  nand nand_3 (nand_3_out, D0_q[2], D0_qn);
  nand nand_4 (nand_4_out, D2_qn, D1_qn, D0_q[0]);
  nand nand_5 (nand_5_out, D0_q[1], D0_qn);
  nand nand_6 (nand_6_out, D0_q[2], D0_qn);
  nand nand_7 (nand_7_out, D2_qn, D0_qn);
  nand nand_8 (nand_8_out, D2_qn, D0_q[1]);
  nand nand_9 (nand_9_out, D0_q[1], D0_qn);
  nand nand_10 (nand_10_out, nand_1_out, nand_2_out, nand_3_out);
  nand nand_11 (nand_11_out, nand_4_out, nand_5_out, nand_6_out);
  nand nand_12 (nand_12_out, nand_7_out, nand_8_out, nand_9_out);
  Clock clock_1 (.out(clock_1_out));
  D_Flip_Flop D2 (.clk(clock_1_out), .D(nand_10_out), .Q(D0_q[2]), .Qn(D2_qn), .reset(reset_out));  // open: preset, en
  D_Flip_Flop D1 (.clk(clock_1_out), .D(nand_11_out), .Q(D0_q[1]), .Qn(D1_qn), .reset(reset_out));  // open: preset, en
  D_Flip_Flop D0 (.clk(clock_1_out), .D(nand_12_out), .Q(D0_q[0]), .Qn(D0_qn), .reset(reset_out));  // open: preset, en
  Button reset (.out(reset_out));
  not not_1 (D0_q[3], 1'b1);
  Hex_Digit_Display hex_digit_display_1 (.value(D0_q));  // open: dp

  // Notes on the sheet:
  //   -Q2
  //   Q1
  //   Q0
  //   Q2
  //   -Q1
  //   Q2
  //   -Q0
  //   -Q2
  //   -Q1
  //   Q0
  //   Q1
  //   -Q0
  //   Q2
  //   -Q0
  //   -Q2
  //   -Q0
  //   -Q2
  //   Q1
  //   Q1
  //   -Q0
endmodule

module x (
  input  in_1
);

  wire and_1_out, clock_1_out, D0_q, D0_qn, D1_q, D1_qn, D2_q, D2_qn, nand_1_out, nand_2_out, nand_3_out,
       nand_4_out, nand_5_out, nand_6_out, nand_7_out, nand_8_out, not_1_out, or_1_out, or_2_out, or_3_out,
       undriven;
  wire [2:0] undriven_2;

  Clock clock_1 (.out(clock_1_out));
  D_Flip_Flop D2 (.clk(clock_1_out), .D(nand_8_out), .Q(D2_q), .Qn(D2_qn));  // open: preset, en, reset
  D_Flip_Flop D1 (.clk(clock_1_out), .D(nand_4_out), .Q(D1_q), .Qn(D1_qn));  // open: preset, en, reset
  D_Flip_Flop D0 (.clk(clock_1_out), .D(or_3_out), .Q(D0_q), .Qn(D0_qn));  // open: preset, en, reset
  or or_1 (or_1_out, undriven, D2_qn);
  nand nand_1 (nand_1_out, D2_qn, D1_q);
  not not_1 (not_1_out, nand_1_out);
  or or_2 (or_2_out, D2_qn, D1_q);
  nand nand_2 (nand_2_out, or_1_out, D0_qn);
  nand nand_3 (nand_3_out, D2_qn, D0_q, D1_qn);
  and and_1 (and_1_out, or_2_out, D0_qn);
  nand nand_4 (nand_4_out, nand_2_out, nand_3_out);
  nand nand_5 (nand_5_out, not_1_out, D0_q);
  nand nand_6 (nand_6_out, D2_q, nand_7_out);
  nand nand_7 (nand_7_out, D1_q, D0_q);
  or or_3 (or_3_out, not_1_out, and_1_out);
  nand nand_8 (nand_8_out, nand_5_out, nand_6_out);
  // Probe on {in_1, undriven_2}
  Hex_Digit_Display hex_digit_display_1 (.value({in_1, undriven_2}));  // open: dp
endmodule

module \nand  (
  input  c,
  input  b,
  input  a,
  output f
);

  wire not_1_out, not_2_out, not_3_out, not_4_out, not_5_out, not_6_out;

  not not_1 (not_1_out, c);
  not not_2 (not_2_out, b);
  not not_3 (not_3_out, a);
  // NOT_Gate not_4 has open pins: in=open, out=not_4_out
  // NOT_Gate not_5 has open pins: in=open, out=not_5_out
  // NOT_Gate not_6 has open pins: in=open, out=not_6_out
  nand nand_1 (f, not_1_out, not_2_out, not_3_out);
  // NAND_Gate nand_2 has open pins: in0=not_4_out, in1=not_5_out, in2=not_6_out, out=open
endmodule
