// Logisim project asyn9.10.11.12.circ as structural Verilog: 1 circuit, main circuit main
module main (
  input  in_1,
  input  in_2,
  input  in_3,
  input  in_4
);

  wire and_1_out, and_2_out, and_3_out, button_1_out, button_2_out, button_3_out, button_4_out, j_k_ff_1_q,
       j_k_ff_2_q, j_k_ff_3_q, j_k_ff_5_q, j_k_ff_6_q, or_1_out;
  wire [3:0] j_k_ff_1_qn;

  Button button_1 (.out(button_1_out));
  J_K_Flip_Flop j_k_ff_1 (
    .J(in_1), .clk(button_1_out), .K(in_1), .Q(j_k_ff_1_q), .Qn(j_k_ff_1_qn[0]));  // open: preset, en, reset
  J_K_Flip_Flop j_k_ff_2 (
    .J(in_1), .clk(j_k_ff_1_q), .K(in_1), .Q(j_k_ff_2_q), .Qn(j_k_ff_1_qn[1]));  // open: preset, en, reset
  J_K_Flip_Flop j_k_ff_3 (
    .J(in_1), .clk(j_k_ff_2_q), .K(in_1), .Q(j_k_ff_3_q), .Qn(j_k_ff_1_qn[2]));  // open: preset, en, reset
  // Probe on j_k_ff_1_qn
  Button button_2 (.out(button_2_out));
  Button button_3 (.out(button_3_out));
  J_K_Flip_Flop j_k_ff_4 (.J(in_1), .clk(j_k_ff_3_q), .K(in_1), .Qn(j_k_ff_1_qn[3]));  // open: Q, preset, en, reset
  Hex_Digit_Display hex_digit_display_1 (.value(j_k_ff_1_qn));  // open: dp
  J_K_Flip_Flop #(.trigger("falling")) j_k_ff_5 (
    .J(in_2), .clk(button_2_out), .K(in_2), .Q(j_k_ff_5_q), .preset(and_1_out), .reset(or_1_out));  // open: Qn, en
  and and_1 (and_1_out, button_3_out, in_3);
  and and_2 (and_2_out, button_3_out, in_4);
  J_K_Flip_Flop #(.trigger("falling")) j_k_ff_6 (
    .J(in_2), .clk(j_k_ff_5_q), .K(in_2), .Q(j_k_ff_6_q), .preset(and_2_out), .reset(or_1_out));  // open: Qn, en
  or or_1 (or_1_out, and_3_out, button_4_out);
  and and_3 (and_3_out, j_k_ff_5_q, j_k_ff_6_q);
  Button button_4 (.out(button_4_out));
endmodule
