// Logisim project jacektopipa.circ as structural Verilog: 1 circuit, main circuit main
module main (
  input  z1,
  input  z0
);

  wire and_1_out, and_2_out, and_3_out, and_4_out, and_5_out, button_1_out, not_1_out, not_2_out, not_3_out,
       not_4_out, not_5_out, not_6_out, not_7_out, not_8_out, not_9_out, not_10_out, not_11_out, or_1_out;
  wire [3:0] q0_q;

  Button button_1 (.out(button_1_out));
  Hex_Digit_Display hex_digit_display_1 (.value(q0_q));  // open: dp
  not not_1 (not_1_out, q0_q[2]);
  not not_2 (not_2_out, q0_q[1]);
  not not_3 (not_3_out, z1);
  not not_4 (not_4_out, z0);
  not not_5 (not_5_out, q0_q[2]);
  not not_6 (not_6_out, q0_q[0]);
  not not_7 (not_7_out, z1);
  not not_8 (not_8_out, q0_q[2]);
  not not_9 (not_9_out, z0);
  not not_10 (not_10_out, q0_q[1]);
  not not_11 (not_11_out, q0_q[0]);
  J_K_Flip_Flop #(.trigger("falling")) q0 (
    .J(1'b1), .clk(button_1_out), .K(1'b1), .Q(q0_q[0]), .reset(and_5_out));  // open: Qn, preset, en
  and and_1 (and_1_out, not_1_out, not_2_out, q0_q[0], not_3_out, not_4_out);
  and and_2 (and_2_out, not_5_out, q0_q[1], not_6_out, not_7_out, z0);
  and and_3 (and_3_out, not_8_out, q0_q[1], q0_q[0], z1, not_9_out);
  and and_4 (and_4_out, q0_q[2], not_10_out, not_11_out, z1, z0);
  J_K_Flip_Flop #(.trigger("falling")) q1 (
    .J(1'b1), .clk(q0_q[0]), .K(1'b1), .Q(q0_q[1]), .reset(and_5_out));  // open: Qn, preset, en
  or or_1 (or_1_out, and_1_out, and_2_out, and_3_out, and_4_out);
  J_K_Flip_Flop #(.trigger("falling")) q2 (
    .J(1'b1), .clk(q0_q[1]), .K(1'b1), .Q(q0_q[2]), .reset(and_5_out));  // open: Qn, preset, en
  and and_5 (and_5_out, q0_q[3], or_1_out);
  J_K_Flip_Flop #(.trigger("falling")) q3 (
    .J(1'b1), .clk(q0_q[2]), .K(1'b1), .Q(q0_q[3]), .reset(and_5_out));  // open: Qn, preset, en
endmodule
