// Logisim project ssijpale.circ as structural Verilog: 1 circuit, main circuit main
module main (
  input  z1,
  input  z0
);

  wire button_1_out, nand_1_out, nand_2_out, nand_3_out, nand_4_out, nand_5_out, nand_6_out, nand_7_out,
       nand_8_out, nand_9_out, nand_10_out, not_1_out, not_2_out, not_3_out, not_4_out, not_5_out, not_6_out,
       not_7_out, not_8_out, not_9_out, not_10_out, not_11_out, not_12_out, not_13_out, not_14_out,
       not_15_out, not_16_out;
  wire [3:0] q0_q;

  Button button_1 (.out(button_1_out));
  not not_1 (not_1_out, q0_q[2]);
  not not_2 (not_2_out, q0_q[1]);
  not not_3 (not_3_out, z1);
  not not_4 (not_4_out, z0);
  not not_5 (not_5_out, q0_q[2]);
  not not_6 (not_6_out, q0_q[0]);
  not not_7 (not_7_out, z1);
  not not_8 (not_8_out, q0_q[2]);
  not not_9 (not_9_out, z0);
  not not_10 (not_10_out, q0_q[1]);
  not not_11 (not_11_out, q0_q[0]);
  J_K_Flip_Flop #(.trigger("falling")) q0 (
    .J(1'b1), .clk(button_1_out), .K(1'b1), .Q(q0_q[0]), .reset(not_16_out));  // open: Qn, preset, en
  nand nand_1 (nand_1_out, not_2_out, q0_q[0], not_3_out, not_4_out);
  nand nand_2 (nand_2_out, q0_q[1], not_6_out, not_7_out, z0);
  nand nand_3 (nand_3_out, q0_q[1], q0_q[0], z1, not_9_out);
  nand nand_4 (nand_4_out, not_10_out, not_11_out, z1, z0);
  J_K_Flip_Flop #(.trigger("falling")) q1 (
    .J(1'b1), .clk(q0_q[0]), .K(1'b1), .Q(q0_q[1]), .reset(not_16_out));  // open: Qn, preset, en
  nand nand_5 (nand_5_out, not_1_out, not_12_out);
  not not_12 (not_12_out, nand_1_out);
  nand nand_6 (nand_6_out, not_5_out, not_13_out);
  not not_13 (not_13_out, nand_2_out);
  nand nand_7 (nand_7_out, not_8_out, not_14_out);
  not not_14 (not_14_out, nand_3_out);
  nand nand_8 (nand_8_out, q0_q[2], not_15_out);
  not not_15 (not_15_out, nand_4_out);
  J_K_Flip_Flop #(.trigger("falling")) q2 (
    .J(1'b1), .clk(q0_q[1]), .K(1'b1), .Q(q0_q[2]), .reset(not_16_out));  // open: Qn, preset, en
  J_K_Flip_Flop #(.trigger("falling")) q3 (
    .J(1'b1), .clk(q0_q[2]), .K(1'b1), .Q(q0_q[3]), .reset(not_16_out));  // open: Qn, preset, en
  nand nand_9 (nand_9_out, nand_5_out, nand_6_out, nand_7_out, nand_8_out);
  nand nand_10 (nand_10_out, q0_q[3], nand_9_out);
  not not_16 (not_16_out, nand_10_out);
  Hex_Digit_Display hex_digit_display_1 (.value(q0_q));  // open: dp
endmodule
