// Logisim project mod16_D.circ as structural Verilog: 1 circuit, main circuit main
module main (
);

  wire button_1_out, D1_2_q, D1_3_q, D1_q;
  wire [3:0] D1_qn;

  Button button_1 (.out(button_1_out));
  D_Flip_Flop D1 (.clk(button_1_out), .D(D1_qn[0]), .Q(D1_q), .Qn(D1_qn[0]));  // open: preset, en, reset
  D_Flip_Flop D1_2 (.clk(D1_q), .D(D1_qn[1]), .Q(D1_2_q), .Qn(D1_qn[1]));  // open: preset, en, reset
  D_Flip_Flop D1_3 (.clk(D1_2_q), .D(D1_qn[2]), .Q(D1_3_q), .Qn(D1_qn[2]));  // open: preset, en, reset
  D_Flip_Flop D1_4 (.clk(D1_3_q), .D(D1_qn[3]), .Qn(D1_qn[3]));  // open: Q, preset, en, reset
  Hex_Digit_Display hex_digit_display_1 (.value(D1_qn));  // open: dp
  // Probe on D1_qn
endmodule
