// Logisim project nastepnik3bitNAND.circ as structural Verilog: 1 circuit, main circuit main
module main (
  input  x2,
  input  x1,
  input  x0,
  output y2,
  output y1,
  output y0
);

  wire nand_1_out, nand_2_out, nand_4_out, nand_5_out, nand_6_out, nand_7_out, nand_8_out, nand_9_out,
       nand_10_out, nand_12_out, nand_13_out;

  nand nand_1 (nand_1_out, x2, x2);
  nand nand_2 (nand_2_out, x1, x1);
  nand nand_3 (y0, x0, x0);
  nand nand_4 (nand_4_out, x2, y0);
  nand nand_5 (nand_5_out, x2, nand_2_out);
  nand nand_6 (nand_6_out, nand_1_out, x1);
  nand nand_7 (nand_7_out, x1, y0);
  nand nand_8 (nand_8_out, nand_2_out, x0);
  nand nand_9 (nand_9_out, nand_4_out, nand_5_out);
  nand nand_10 (nand_10_out, nand_6_out, nand_6_out);
  nand nand_11 (y1, nand_7_out, nand_8_out);
  nand nand_12 (nand_12_out, nand_9_out, nand_9_out);
  nand nand_13 (nand_13_out, nand_10_out, x0);
  nand nand_14 (y2, nand_12_out, nand_13_out);
endmodule
