// Logisim project newluc.circ as structural Verilog: 1 circuit, main circuit main
module main (
);

  wire and_1_out, and_2_out, not_1_out, not_2_out, not_3_out, not_4_out, not_5_out, or_1_out, or_2_out,
       or_3_out, or_4_out, or_5_out, or_6_out, or_7_out, or_8_out, or_9_out, or_10_out, or_11_out, or_12_out,
       Q0_out, Q1_out, Q2_out, z0_out, z1_out;

  Button z1 (.out(z1_out));
  Button z0 (.out(z0_out));
  not not_1 (not_1_out, z1_out);
  not not_2 (not_2_out, z0_out);
  or or_1 (or_1_out, z1_out, Q1_out);
  or or_2 (or_2_out, Q2_out, z1_out);
  or or_3 (or_3_out, Q1_out, Q2_out);
  or or_4 (or_4_out, not_1_out, Q0_out, not_3_out);
  or or_5 (or_5_out, Q1_out, not_1_out);
  or or_6 (or_6_out, Q0_out, Q1_out);
  or or_7 (or_7_out, z1_out, Q0_out, Q1_out);
  or or_8 (or_8_out, not_4_out, Q1_out);
  or or_9 (or_9_out, not_3_out, Q0_out);
  or or_10 (or_10_out, not_4_out, z1_out);
  not not_3 (not_3_out, Q1_out);
  not not_4 (not_4_out, Q2_out);
  and Q2 (Q2_out, or_1_out, or_2_out, or_3_out, not_2_out);
  and Q1 (Q1_out, or_4_out, or_5_out, or_6_out, not_2_out);
  and Q0 (Q0_out, or_7_out, or_8_out, or_10_out, or_9_out, not_2_out);
  not not_5 (not_5_out, Q2_out);
  and and_1 (and_1_out, Q2_out, Q1_out);
  or or_11 (or_11_out, Q2_out, Q0_out);
  or or_12 (or_12_out, not_5_out, Q1_out);
  LED Y1 (.in(and_1_out));
  and and_2 (and_2_out, or_11_out, or_12_out);
  LED Y0 (.in(and_2_out));
endmodule
