// Logisim project pamiec4x1.circ as structural Verilog: 2 circuits, main circuit main
module main (
  input  X,
  input  A1,
  input  A0
);

  wire and_1_out, and_2_out, and_3_out, and_4_out, and_5_out, and_6_out, and_7_out, and_8_out, button_1_out,
       d_ff_1_q, d_ff_2_q, d_ff_3_q, d_ff_4_q, not_1_out, not_2_out, or_1_out;

  Button button_1 (.out(button_1_out));
  not not_1 (not_1_out, A1);
  not not_2 (not_2_out, A0);
  and and_1 (and_1_out, not_2_out, not_1_out, button_1_out);
  and and_2 (and_2_out, A0, not_1_out, button_1_out);
  D_Flip_Flop d_ff_1 (.clk(and_1_out), .D(X), .Q(d_ff_1_q));  // open: Qn, preset, en, reset
  and and_3 (and_3_out, not_2_out, not_1_out, d_ff_1_q);
  and and_4 (and_4_out, A0, not_1_out, d_ff_2_q);
  or or_1 (or_1_out, and_3_out, and_4_out, and_7_out, and_6_out);
  LED led_1 (.in(or_1_out));
  and and_5 (and_5_out, not_2_out, A1, button_1_out);
  D_Flip_Flop d_ff_2 (.clk(and_2_out), .D(X), .Q(d_ff_2_q));  // open: Qn, preset, en, reset
  and and_6 (and_6_out, A0, A1, d_ff_4_q);
  and and_7 (and_7_out, not_2_out, A1, d_ff_3_q);
  and and_8 (and_8_out, A0, A1, button_1_out);
  D_Flip_Flop d_ff_3 (.clk(and_5_out), .D(X), .Q(d_ff_3_q));  // open: Qn, preset, en, reset
  D_Flip_Flop d_ff_4 (.clk(and_8_out), .D(X), .Q(d_ff_4_q));  // open: Qn, preset, en, reset
endmodule

module \nand  (
  input  X,
  input  A1,
  input  A0
);

  wire button_1_out, d_ff_1_q, d_ff_2_q, d_ff_3_q, d_ff_4_q, nand_1_out, nand_2_out, nand_3_out, nand_4_out,
       nand_5_out, nand_6_out, nand_7_out, nand_8_out, nand_9_out, not_1_out, not_2_out;

  Button button_1 (.out(button_1_out));
  not not_1 (not_1_out, A1);
  not not_2 (not_2_out, A0);
  nand nand_1 (nand_1_out, not_2_out, not_1_out, button_1_out);
  nand nand_2 (nand_2_out, A0, not_1_out, button_1_out);
  D_Flip_Flop d_ff_1 (.clk(nand_1_out), .D(X), .Q(d_ff_1_q));  // open: Qn, preset, en, reset
  nand nand_3 (nand_3_out, A0, not_1_out, d_ff_2_q);
  nand nand_4 (nand_4_out, not_2_out, not_1_out, d_ff_1_q);
  nand nand_5 (nand_5_out, nand_4_out, nand_3_out, nand_8_out, nand_7_out);
  LED led_1 (.in(nand_5_out));
  nand nand_6 (nand_6_out, not_2_out, A1, button_1_out);
  D_Flip_Flop d_ff_2 (.clk(nand_2_out), .D(X), .Q(d_ff_2_q));  // open: Qn, preset, en, reset
  nand nand_7 (nand_7_out, A0, A1, d_ff_4_q);
  nand nand_8 (nand_8_out, not_2_out, A1, d_ff_3_q);
  nand nand_9 (nand_9_out, A0, A1, button_1_out);
  D_Flip_Flop d_ff_3 (.clk(nand_6_out), .D(X), .Q(d_ff_3_q));  // open: Qn, preset, en, reset
  D_Flip_Flop d_ff_4 (.clk(nand_9_out), .D(X), .Q(d_ff_4_q));  // open: Qn, preset, en, reset
endmodule
