// Logisim project parametryczny.circ as structural Verilog: 1 circuit, main circuit main
module main (
  input  s1,
  input  p,
  input  s0,
  input  z
);

  wire b0_q, b0_qn, b1_q, clock_out, nand_1_out, nand_2_out, nand_3_out, nand_5_out, nand_6_out, nand_7_out,
       nand_8_out, nand_9_out, nand_10_out, nand_11_out, nand_12_out, nand_13_out, nand_14_out, nand_15_out,
       nand_16_out, nand_17_out, not_1_out, not_2_out, not_3_out, not_4_out, not_5_out, not_6_out, reset_out,
       s1_out;

  not not_1 (not_1_out, s1);
  not not_2 (not_2_out, p);
  not not_3 (not_3_out, z);
  not not_4 (not_4_out, not_3_out);
  nand nand_1 (nand_1_out, not_2_out, not_3_out, not_1_out, b0_qn);
  nand nand_2 (nand_2_out, p, z, not_1_out);
  nand nand_3 (nand_3_out, p, z, b0_qn);
  // NAND_Gate nand_4 has open pins: in0=not_2_out, in1=not_4_out, in2=not_1_out, in3=b0_q, out=open
  not u_s1 (s1_out, not_1_out);
  not not_5 (not_5_out, s0);
  // NAND_Gate s0 has open pins: in0=nand_1_out, in1=nand_2_out, in2=nand_3_out, out=open
  nand nand_5 (nand_5_out, not_1_out, b0_qn);
  nand nand_6 (nand_6_out, b0_qn, not_5_out);
  nand nand_7 (nand_7_out, not_1_out, s0, not_1_out);
  nand nand_8 (nand_8_out, b1_q, b0_qn, not_5_out, not_1_out);
  nand nand_9 (nand_9_out, not_1_out, not_1_out, s0);
  nand nand_10 (nand_10_out, not_1_out, not_5_out, s1_out);
  nand nand_11 (nand_11_out, not_1_out, b0_q, not_1_out, s0);
  nand nand_12 (nand_12_out, nand_5_out, nand_6_out);
  nand nand_13 (nand_13_out, nand_7_out, nand_8_out);
  nand nand_14 (nand_14_out, nand_9_out, nand_10_out);
  not not_6 (not_6_out, nand_11_out);
  Button clock (.out(clock_out));
  J_K_Flip_Flop b1 (
    .J(not_6_out), .clk(clock_out), .K(nand_12_out), .Q(b1_q), .Qn(not_1_out), .reset(reset_out));  // open: preset, en
  J_K_Flip_Flop b0 (
    .J(nand_13_out), .clk(clock_out), .K(nand_14_out), .Q(b0_q), .Qn(b0_qn), .reset(reset_out));  // open: preset, en
  Button reset (.out(reset_out));
  nand nand_15 (nand_15_out, not_2_out, b0_q, not_1_out);
  nand nand_16 (nand_16_out, p, b0_qn);
  nand nand_17 (nand_17_out, nand_15_out, nand_16_out);
  LED led_1 (.in(nand_17_out));
endmodule
