// Logisim project register.circ as structural Verilog: 1 circuit, main circuit main
module main (
  input  in_1,
  input  in_2,
  input  in_3,
  input  in_4,
  input  in_5
);

  wire and_1_out, and_2_out, and_3_out, and_4_out, clocl_out, d_ff_1_q, d_ff_2_q, d_ff_3_q, d_ff_4_q, in_out,
       reset_out;

  Button clocl (.out(clocl_out));
  Button reset (.out(reset_out));
  and and_1 (and_1_out, in_out, in_2);
  Button in (.out(in_out));
  LED led_1 (.in(d_ff_1_q));
  D_Flip_Flop d_ff_1 (.clk(clocl_out), .D(in_1), .Q(d_ff_1_q), .preset(and_1_out), .reset(reset_out));  // open: Qn, en
  and and_2 (and_2_out, in_out, in_3);
  LED led_2 (.in(d_ff_2_q));
  D_Flip_Flop d_ff_2 (
    .clk(clocl_out), .D(d_ff_1_q), .Q(d_ff_2_q), .preset(and_2_out), .reset(reset_out));  // open: Qn, en
  and and_3 (and_3_out, in_out, in_4);
  LED led_3 (.in(d_ff_3_q));
  D_Flip_Flop d_ff_3 (
    .clk(clocl_out), .D(d_ff_2_q), .Q(d_ff_3_q), .preset(and_3_out), .reset(reset_out));  // open: Qn, en
  and and_4 (and_4_out, in_out, in_5);
  LED led_4 (.in(d_ff_4_q));
  D_Flip_Flop d_ff_4 (
    .clk(clocl_out), .D(d_ff_3_q), .Q(d_ff_4_q), .preset(and_4_out), .reset(reset_out));  // open: Qn, en
endmodule
