// Logisim project s1s0-parametryczny-siatki.circ as structural Verilog: 1 circuit, main circuit main
module main (
  input  p,
  input  z,
  input  b1,
  input  b0,
  output s1,
  output s0
);

  wire nand_1_out, nand_2_out, nand_3_out, nand_4_out, nand_5_out, nand_6_out, nand_7_out, nand_8_out,
       nand_9_out, nand_10_out, nand_11_out, nand_12_out;

  nand nand_1 (nand_1_out, p, p);
  nand nand_2 (nand_2_out, b1, b1);
  nand nand_3 (nand_3_out, p, p);
  nand nand_4 (nand_4_out, z, z);
  nand nand_5 (nand_5_out, b1, b1);
  nand nand_6 (nand_6_out, b0, b0);
  nand nand_7 (nand_7_out, b1, b1);
  nand nand_8 (nand_8_out, b0, b0);
  nand nand_9 (nand_9_out, nand_1_out, z, nand_2_out, b0);
  nand nand_10 (nand_10_out, nand_3_out, nand_4_out, nand_5_out, nand_6_out);
  nand nand_11 (nand_11_out, p, z, nand_7_out);
  nand nand_12 (nand_12_out, p, z, nand_8_out);
  nand nand_13 (s1, nand_9_out, nand_9_out);
  nand nand_14 (s0, nand_10_out, nand_11_out, nand_12_out);
endmodule
