// Logisim project sumator-akum.circ as structural Verilog: 1 circuit, main circuit main
module main (
  input  in_1,
  input  in_2,
  input  in_3,
  input  in_4,
  input  in_5,
  input  in_6,
  input  in_7,
  input  in_8,
  input  in_9,
  input  in_10,
  input  in_11
);

  wire adder_1_cout, adder_1_out, adder_2_cout, adder_2_out, clocl_2_out, clocl_out, d_ff_1_q, d_ff_2_q,
       d_ff_3_q, d_ff_4_q, shift_register_2_out, shift_register_3_out;

  Button clocl (.out(clocl_out));
  Shift_Register #(.length(4), .trigger("falling")) shift_register_1 (
    .in(adder_1_out), .clk(clocl_out));  // open: shift, out, load, clr, d0, q0, d1, q1, d2, q2, d3, q3
  Shift_Register #(.length(4), .trigger("falling")) shift_register_2 (
    .in(adder_1_out), .clk(clocl_out), .out(shift_register_2_out), .load(in_10), .d0(in_1), .d1(in_2),
    .d2(in_3), .d3(in_4));  // open: shift, clr, q0, q1, q2, q3
  Shift_Register #(.length(4), .trigger("falling")) shift_register_3 (
    .clk(clocl_out), .out(shift_register_3_out), .load(in_10), .d0(in_6), .d1(in_7), .d2(in_8), .d3(in_9));  // open: shift, in, clr, q0, q1, q2, q3
  Adder #(.width(1)) adder_1 (
    .a(shift_register_2_out), .b(shift_register_3_out), .out(adder_1_out), .cin(d_ff_1_q), .cout(adder_1_cout));
  D_Flip_Flop d_ff_1 (.clk(clocl_out), .D(adder_1_cout), .Q(d_ff_1_q));  // open: Qn, preset, en, reset
  Button clocl_2 (.out(clocl_2_out));
  Shift_Register #(.length(4)) shift_register_4 (
    .in(adder_2_out), .clk(clocl_2_out));  // open: shift, out, load, clr, d0, q0, d1, q1, d2, q2, d3, q3
  D_Flip_Flop d_ff_2 (.clk(clocl_2_out), .D(in_5), .Q(d_ff_2_q));  // open: Qn, preset, en, reset
  D_Flip_Flop d_ff_3 (.clk(clocl_2_out), .D(in_11), .Q(d_ff_3_q));  // open: Qn, preset, en, reset
  Adder #(.width(1)) adder_2 (.a(d_ff_2_q), .b(d_ff_3_q), .out(adder_2_out), .cin(d_ff_4_q), .cout(adder_2_cout));
  D_Flip_Flop d_ff_4 (.clk(clocl_2_out), .D(adder_2_cout), .Q(d_ff_4_q));  // open: Qn, preset, en, reset
endmodule
