// Logisim project sumator_szeregowy.circ as structural Verilog: 1 circuit, main circuit main
module main (
  input  z1,
  input  z0
);

  wire clock_1_out, d_ff_1_q, j_k_ff_1_q, j_k_ff_1_qn, nand_1_out, nand_2_out, nand_3_out, nand_4_out,
       nand_5_out, nand_6_out, nand_7_out, not_1_out, not_2_out, not_3_out, not_4_out, reset_out;

  not not_1 (not_1_out, z1);
  nand nand_1 (nand_1_out, z1, z0);
  not not_2 (not_2_out, z0);
  not not_3 (not_3_out, nand_1_out);
  Clock clock_1 (.out(clock_1_out));
  nand nand_2 (nand_2_out, not_1_out, not_2_out);
  J_K_Flip_Flop j_k_ff_1 (
    .J(not_3_out), .clk(clock_1_out), .K(not_4_out), .Q(j_k_ff_1_q), .Qn(j_k_ff_1_qn), .reset(reset_out));  // open: preset, en
  not not_4 (not_4_out, nand_2_out);
  Button reset (.out(reset_out));
  nand nand_3 (nand_3_out, z0, j_k_ff_1_qn, not_1_out);
  nand nand_4 (nand_4_out, z1, j_k_ff_1_qn, not_2_out);
  nand nand_5 (nand_5_out, j_k_ff_1_q, not_2_out, not_1_out);
  nand nand_6 (nand_6_out, z1, j_k_ff_1_q, z0);
  nand nand_7 (nand_7_out, nand_3_out, nand_4_out, nand_5_out, nand_6_out);
  D_Flip_Flop d_ff_1 (.clk(clock_1_out), .D(nand_7_out), .Q(d_ff_1_q), .reset(reset_out));  // open: Qn, preset, en
  LED led_1 (.in(d_ff_1_q));
endmodule
