// Logisim project tty.circ as structural Verilog: 1 circuit, main circuit main
module main (
  input  in_1,
  input  in_2,
  input  in_3,
  input  in_4,
  input  in_5,
  input  in_6,
  input  in_7
);

  wire button_1_out;

  // Probe on {in_1, in_2, in_3, in_4, in_5, in_6, in_7}
  Button button_1 (.out(button_1_out));
  TTY tty_1 (.data({in_1, in_2, in_3, in_4, in_5, in_6, in_7}), .clk(button_1_out));  // open: we, clr
endmodule
