// Logisim project y-parametryczny-siatki.circ as structural Verilog: 1 circuit, main circuit main
module main (
  input  p,
  input  q1,
  input  q0,
  output y
);

  wire nand_1_out, nand_2_out, nand_3_out, nand_4_out, nand_5_out;

  nand nand_1 (nand_1_out, p, p);
  nand nand_2 (nand_2_out, q1, q1);
  nand nand_3 (nand_3_out, q0, q0);
  nand nand_4 (nand_4_out, nand_1_out, nand_2_out, q0);
  nand nand_5 (nand_5_out, p, nand_3_out);
  nand nand_6 (y, nand_4_out, nand_5_out);
endmodule
